// Logisim project Lab5.circ as structural Verilog: 7 circuits, main circuit main
module main (
  input  res,
  input  [2:0] in_2,
  output [3:0] out_3
);

  wire clk_out;

  Clock #(.highDuration(4), .lowDuration(4)) clk (.out(clk_out));
  Clock sysclk ();  // open: out
  Universal universal_1 (.in_1(clk_out), .in_2(res), .in_3(in_2), .out_4(out_3));

  // Notes on the sheet:
  //   Up - 000
  //   Down - 001
  //   Dec - 010
  //   Ring - 011
  //   Johnson - 100
endmodule

module Up (
  input  in_1,
  input  in_2,
  output [3:0] out_3
);

  wire d_ff_1_qn, d_ff_2_qn, d_ff_3_qn, d_ff_4_qn;

  D_Flip_Flop d_ff_1 (.D(d_ff_1_qn), .clk(in_1), .Q(out_3[0]), .Qn(d_ff_1_qn), .reset(in_2));  // open: preset
  D_Flip_Flop d_ff_2 (.D(d_ff_2_qn), .clk(d_ff_1_qn), .Q(out_3[1]), .Qn(d_ff_2_qn), .reset(in_2));  // open: preset
  D_Flip_Flop d_ff_3 (.D(d_ff_3_qn), .clk(d_ff_2_qn), .Q(out_3[2]), .Qn(d_ff_3_qn), .reset(in_2));  // open: preset
  D_Flip_Flop d_ff_4 (.D(d_ff_4_qn), .clk(d_ff_3_qn), .Q(out_3[3]), .Qn(d_ff_4_qn), .reset(in_2));  // open: preset
endmodule

module Down (
  input  in_1,
  input  in_2,
  output [3:0] out_3
);

  wire d_ff_1_qn, d_ff_2_qn, d_ff_3_qn, d_ff_4_qn;

  D_Flip_Flop d_ff_1 (.D(d_ff_1_qn), .clk(in_1), .Q(out_3[0]), .Qn(d_ff_1_qn), .preset(in_2));  // open: reset
  D_Flip_Flop d_ff_2 (.D(d_ff_2_qn), .clk(out_3[0]), .Q(out_3[1]), .Qn(d_ff_2_qn), .preset(in_2));  // open: reset
  D_Flip_Flop d_ff_3 (.D(d_ff_3_qn), .clk(out_3[1]), .Q(out_3[2]), .Qn(d_ff_3_qn), .preset(in_2));  // open: reset
  D_Flip_Flop d_ff_4 (.D(d_ff_4_qn), .clk(out_3[2]), .Q(out_3[3]), .Qn(d_ff_4_qn), .preset(in_2));  // open: reset
endmodule

module Decade (
  input  in_1,
  input  in_2,
  output [3:0] out_3
);

  wire and_1_out, d_ff_1_qn, d_ff_2_qn, d_ff_3_qn, d_ff_4_qn, or_1_out;

  D_Flip_Flop d_ff_1 (.D(d_ff_1_qn), .clk(in_1), .Q(out_3[0]), .Qn(d_ff_1_qn), .reset(or_1_out));  // open: preset
  or or_1 (or_1_out, in_2, and_1_out);
  D_Flip_Flop d_ff_2 (.D(d_ff_2_qn), .clk(d_ff_1_qn), .Q(out_3[1]), .Qn(d_ff_2_qn), .reset(or_1_out));  // open: preset
  D_Flip_Flop d_ff_3 (.D(d_ff_3_qn), .clk(d_ff_2_qn), .Q(out_3[2]), .Qn(d_ff_3_qn), .reset(or_1_out));  // open: preset
  D_Flip_Flop d_ff_4 (.D(d_ff_4_qn), .clk(d_ff_3_qn), .Q(out_3[3]), .Qn(d_ff_4_qn), .reset(or_1_out));  // open: preset
  and and_1 (and_1_out, out_3[3], out_3[1]);
endmodule

module Ring (
  input  in_1,
  input  in_2,
  output [3:0] out_3
);

  D_Flip_Flop d_ff_1 (.D(out_3[3]), .clk(in_1), .Q(out_3[0]), .preset(in_2));  // open: Qn, reset
  D_Flip_Flop d_ff_2 (.D(out_3[0]), .clk(in_1), .Q(out_3[1]), .reset(in_2));  // open: Qn, preset
  D_Flip_Flop d_ff_3 (.D(out_3[1]), .clk(in_1), .Q(out_3[2]), .reset(in_2));  // open: Qn, preset
  D_Flip_Flop d_ff_4 (.D(out_3[2]), .clk(in_1), .Q(out_3[3]), .reset(in_2));  // open: Qn, preset
endmodule

module Johnson (
  input  in_1,
  input  in_2,
  output [3:0] out_3
);

  wire d_ff_4_qn;

  D_Flip_Flop d_ff_1 (.D(d_ff_4_qn), .clk(in_1), .Q(out_3[0]), .preset(in_2));  // open: Qn, reset
  D_Flip_Flop d_ff_2 (.D(out_3[0]), .clk(in_1), .Q(out_3[1]), .reset(in_2));  // open: Qn, preset
  D_Flip_Flop d_ff_3 (.D(out_3[1]), .clk(in_1), .Q(out_3[2]), .reset(in_2));  // open: Qn, preset
  D_Flip_Flop d_ff_4 (.D(out_3[2]), .clk(in_1), .Q(out_3[3]), .Qn(d_ff_4_qn), .reset(in_2));  // open: preset
endmodule

module Universal (
  input  in_1,
  input  in_2,
  input  [2:0] in_3,
  output [3:0] out_4
);

  wire [3:0] decade_1_out_3, down_1_out_3, johnson_1_out_3, ring_1_out_3, up_1_out_3;

  Up up_1 (.in_1(in_1), .in_2(in_2), .out_3(up_1_out_3));
  Down down_1 (.in_1(in_1), .in_2(in_2), .out_3(down_1_out_3));
  Decade decade_1 (.in_1(in_1), .in_2(in_2), .out_3(decade_1_out_3));
  Ring ring_1 (.in_1(in_1), .in_2(in_2), .out_3(ring_1_out_3));
  Johnson johnson_1 (.in_1(in_1), .in_2(in_2), .out_3(johnson_1_out_3));
  Multiplexer #(.select(3), .width(4)) multiplexer_1 (
    .in0(up_1_out_3), .in1(down_1_out_3), .in2(decade_1_out_3), .in3(ring_1_out_3), .in4(johnson_1_out_3),
    .out(out_4), .sel(in_3));  // open: in5, in6, in7
endmodule
